# Fritzing sketch BreathingLed (saved by Fritzing 0.7.0b)
breadboards: 1

parts:
  Arduino1 = Arduino
  R1 = Resistor [tolerance=±5% resistance=220 package=THT]
  LED1 = LED - 3mm [color="Red (633nm)" package="3 mm [THT]"]

nets:
  N1: Arduino1.D3, R1.Pin_0
  N2: Arduino1.GND, LED1.cathode
  N3: R1.Pin_1, LED1.anode
