# Fritzing sketch BreathingLedPot (saved by Fritzing 0.7.0b)
breadboards: 1

parts:
  Arduino1 = Arduino
  R1 = Resistor [tolerance=±5% resistance=220 package=THT]
  LED1 = LED - 3mm [color="Red (633nm)" package="3 mm [THT]"]
  R2 = Rotary Potentiometer (Small) [maximum_resistance=100kΩ]

nets:
  N1: Arduino1.D3, R1.Pin_0
  N2: Arduino1.+5V, R2.leg2
  N3: Arduino1.GND, LED1.cathode, R2.leg1
  N4: Arduino1.A0, R2.wiper
  N5: R1.Pin_1, LED1.anode
