# Fritzing sketch Buzzer (saved by Fritzing 0.7.0b)
breadboards: 1

parts:
  Arduino1 = Arduino
  R1 = Resistor [tolerance=±5% resistance=220 package=THT]
  SPKR1 = Loudspeaker

nets:
  N1: Arduino1.D8, R1.Pin_0
  N2: Arduino1.GND, SPKR1.pin1
  N3: R1.Pin_1, SPKR1.pin2
