# Fritzing sketch Clock_7seg (saved by Fritzing 0.7.0b)
breadboards: 1

parts:
  Arduino1 = Arduino
  DI1 = 7-Segment LED Display [package=THT]
  R1 = Resistor [tolerance=±5% resistance=220 package=THT]
  R2 = Resistor [tolerance=±5% resistance=220 package=THT]
  R3 = Resistor [tolerance=±5% resistance=220 package=THT]
  R4 = Resistor [tolerance=±5% resistance=220 package=THT]
  R5 = Resistor [tolerance=±5% resistance=220 package=THT]
  R6 = Resistor [tolerance=±5% resistance=220 package=THT]
  R7 = Resistor [tolerance=±5% resistance=220 package=THT]
  R8 = Resistor [tolerance=±5% resistance=220 package=THT]

nets:
  N1: Arduino1.D9, R1.Pin_1
  N2: Arduino1.D8, R7.Pin_0
  N3: Arduino1.D7, R8.Pin_0
  N4: Arduino1.D6, R3.Pin_0
  N5: Arduino1.D5, R4.Pin_0
  N6: Arduino1.D4, R2.Pin_1
  N7: Arduino1.D3, R5.Pin_1
  N8: Arduino1.D2, R6.Pin_1
  N9: Arduino1.GND, DI1.commAnode
  N10: DI1.cathodeE, R3.Pin_1
  N11: DI1.cathodeD, R4.Pin_1
  N12: DI1.cathodeC, R2.Pin_0
  N13: DI1.cathodeDP, R1.Pin_0
  N14: DI1.cathodeB, R5.Pin_0
  N15: DI1.cathodeA, R6.Pin_0
  N16: DI1.cathodeF, R8.Pin_1
  N17: DI1.cathodeG, R7.Pin_1
