# Fritzing sketch LCD (saved by Fritzing 0.7.0b)
breadboards: 1

parts:
  Arduino1 = Arduino
  R1 = Rotary Potentiometer (Small) [maximum_resistance=100kΩ]
  LCD1 = LCD screen

nets:
  N1: Arduino1.D12, LCD1.RS
  N2: Arduino1.D11, LCD1.E
  N3: Arduino1.D5, LCD1.DB7
  N4: Arduino1.D4, LCD1.DB6
  N5: Arduino1.D3, LCD1.DB5
  N6: Arduino1.D2, LCD1.DB4
  +5V: Arduino1.+5V, R1.leg2, LCD1.VDD
  GND: Arduino1.GND, R1.leg1, LCD1.VSS, LCD1.R/W
  N7: R1.wiper, LCD1.V0
