# Fritzing sketch LedArray (saved by Fritzing 0.7.0b)
breadboards: 1

parts:
  Arduino1 = Arduino
  R1 = Resistor [tolerance=±5% resistance=220 package=THT]
  R2 = Resistor [tolerance=±5% resistance=220 package=THT]
  R3 = Resistor [tolerance=±5% resistance=220 package=THT]
  R5 = Resistor [tolerance=±5% resistance=220 package=THT]
  R6 = Resistor [tolerance=±5% resistance=220 package=THT]
  R7 = Resistor [tolerance=±5% resistance=220 package=THT]
  R8 = Resistor [tolerance=±5% resistance=220 package=THT]
  R9 = Resistor [tolerance=±5% resistance=220 package=THT]
  R10 = Resistor [tolerance=±5% resistance=220 package=THT]
  R11 = Resistor [tolerance=±5% resistance=220 package=THT]
  R12 = Resistor [tolerance=±5% resistance=220 package=THT]
  R13 = Resistor [tolerance=±5% resistance=220 package=THT]
  R14 = Resistor [tolerance=±5% resistance=220 package=THT]
  R15 = Resistor [tolerance=±5% resistance=220 package=THT]
  R16 = Resistor [tolerance=±5% resistance=220 package=THT]
  LED1 = LED - 5mm [color="Red (633nm)" package="5 mm [THT]"]
  LED2 = LED - 5mm [color="Red (633nm)" package="5 mm [THT]"]
  LED4 = LED - 5mm [color="Red (633nm)" package="5 mm [THT]"]
  LED5 = LED - 5mm [color="Red (633nm)" package="5 mm [THT]"]
  LED6 = LED - 5mm [color="Red (633nm)" package="5 mm [THT]"]
  LED7 = LED - 5mm [color="Red (633nm)" package="5 mm [THT]"]
  LED8 = LED - 5mm [color="Red (633nm)" package="5 mm [THT]"]
  LED9 = LED - 5mm [color="Red (633nm)" package="5 mm [THT]"]
  LED10 = LED - 5mm [color="Red (633nm)" package="5 mm [THT]"]
  LED11 = LED - 5mm [color="Red (633nm)" package="5 mm [THT]"]
  LED12 = LED - 5mm [color="Red (633nm)" package="5 mm [THT]"]
  LED13 = LED - 5mm [color="Red (633nm)" package="5 mm [THT]"]
  LED14 = LED - 5mm [color="Red (633nm)" package="5 mm [THT]"]
  LED15 = LED - 5mm [color="Red (633nm)" package="5 mm [THT]"]
  LED16 = LED - 5mm [color="Red (633nm)" package="5 mm [THT]"]
  R17 = Resistor [tolerance=±5% resistance=220 package=THT]
  LED17 = LED - 5mm [color="Red (633nm)" package="5 mm [THT]"]

nets:
  N1: Arduino1.GND, R17.Pin_0
  N2: Arduino1.D13, LED15.anode
  N3: Arduino1.D12, LED14.anode
  N4: Arduino1.D11, LED13.anode
  N5: Arduino1.D10, LED1.anode
  N6: Arduino1.D9, LED2.anode
  N7: Arduino1.D8, LED4.anode
  N8: Arduino1.D7, LED16.anode
  N9: Arduino1.D6, LED5.anode
  N10: Arduino1.D5, LED6.anode
  N11: Arduino1.D4, LED7.anode
  N12: Arduino1.D3, LED8.anode
  N13: Arduino1.D2, LED9.anode
  N14: Arduino1.A0, LED10.anode
  N15: Arduino1.A1, LED11.anode
  N16: Arduino1.A2, LED12.anode
  N17: Arduino1.A3, LED17.anode
  N18: R1.Pin_0, R2.Pin_0, R3.Pin_0, R5.Pin_0, R6.Pin_0, R7.Pin_0, R8.Pin_0, R9.Pin_0, R10.Pin_0, R11.Pin_0, R12.Pin_0, R13.Pin_0, R14.Pin_0, R15.Pin_0, R16.Pin_0
  N19: R1.Pin_1, LED1.cathode
  N20: R2.Pin_1, LED2.cathode
  N21: R3.Pin_1, LED13.cathode
  N22: R5.Pin_1, LED4.cathode
  N23: R6.Pin_1, LED16.cathode
  N24: R7.Pin_1, LED11.cathode
  N25: R8.Pin_1, LED5.cathode
  N26: R9.Pin_1, LED12.cathode
  N27: R10.Pin_1, LED6.cathode
  N28: R11.Pin_1, LED7.cathode
  N29: R12.Pin_1, LED14.cathode
  N30: R13.Pin_1, LED8.cathode
  N31: R14.Pin_1, LED15.cathode
  N32: R15.Pin_1, LED9.cathode
  N33: R16.Pin_1, LED10.cathode
  N34: R17.Pin_1, LED17.cathode
