# Fritzing sketch LedArray595_16 (saved by Fritzing 0.7.0b)
breadboards: 2

parts:
  Arduino1 = Arduino
  R1 = Resistor [tolerance=±5% resistance=220 package=THT]
  R2 = Resistor [tolerance=±5% resistance=220 package=THT]
  R3 = Resistor [tolerance=±5% resistance=220 package=THT]
  R5 = Resistor [tolerance=±5% resistance=220 package=THT]
  R6 = Resistor [tolerance=±5% resistance=220 package=THT]
  R7 = Resistor [tolerance=±5% resistance=220 package=THT]
  R8 = Resistor [tolerance=±5% resistance=220 package=THT]
  R9 = Resistor [tolerance=±5% resistance=220 package=THT]
  R10 = Resistor [tolerance=±5% resistance=220 package=THT]
  R11 = Resistor [tolerance=±5% resistance=220 package=THT]
  R12 = Resistor [tolerance=±5% resistance=220 package=THT]
  R13 = Resistor [tolerance=±5% resistance=220 package=THT]
  R14 = Resistor [tolerance=±5% resistance=220 package=THT]
  R15 = Resistor [tolerance=±5% resistance=220 package=THT]
  R16 = Resistor [tolerance=±5% resistance=220 package=THT]
  LED1 = LED - 5mm [color="Red (633nm)" package="5 mm [THT]"]
  LED2 = LED - 5mm [color="Red (633nm)" package="5 mm [THT]"]
  LED4 = LED - 5mm [color="Red (633nm)" package="5 mm [THT]"]
  LED5 = LED - 5mm [color="Red (633nm)" package="5 mm [THT]"]
  LED6 = LED - 5mm [color="Red (633nm)" package="5 mm [THT]"]
  LED7 = LED - 5mm [color="Red (633nm)" package="5 mm [THT]"]
  LED8 = LED - 5mm [color="Red (633nm)" package="5 mm [THT]"]
  LED9 = LED - 5mm [color="Red (633nm)" package="5 mm [THT]"]
  LED10 = LED - 5mm [color="Red (633nm)" package="5 mm [THT]"]
  LED11 = LED - 5mm [color="Red (633nm)" package="5 mm [THT]"]
  LED12 = LED - 5mm [color="Red (633nm)" package="5 mm [THT]"]
  LED13 = LED - 5mm [color="Red (633nm)" package="5 mm [THT]"]
  LED14 = LED - 5mm [color="Red (633nm)" package="5 mm [THT]"]
  LED15 = LED - 5mm [color="Red (633nm)" package="5 mm [THT]"]
  LED16 = LED - 5mm [color="Red (633nm)" package="5 mm [THT]"]
  R17 = Resistor [tolerance=±5% resistance=220 package=THT]
  LED17 = LED - 5mm [color="Red (633nm)" package="5 mm [THT]"]
  U1 = 74HC595 [package="DIP16 [THT]"]
  U2 = 74HC595 [package="DIP16 [THT]"]

nets:
  N1: Arduino1.D4, U1.Q3, U2.Q3
  N2: Arduino1.D3, U1.Q4, U2.Q4
  N3: Arduino1.D2, U1.Q6
  N4: Arduino1.+5V, R17.Pin_0
  N5: R1.Pin_0, R2.Pin_0, R3.Pin_0, R5.Pin_0, R6.Pin_0, R7.Pin_0, R8.Pin_0, R9.Pin_0, R10.Pin_0, R11.Pin_0, R12.Pin_0, R13.Pin_0, R14.Pin_0, R15.Pin_0, R16.Pin_0
  N6: R1.Pin_1, LED1.cathode
  N7: R2.Pin_1, LED2.cathode
  N8: R3.Pin_1, LED13.cathode
  N9: R5.Pin_1, LED4.cathode
  N10: R6.Pin_1, LED16.cathode
  N11: R7.Pin_1, LED11.cathode
  N12: R8.Pin_1, LED5.cathode, U2.Q7
  N13: R9.Pin_1, LED12.cathode
  N14: R10.Pin_1, LED6.cathode
  N15: R11.Pin_1, LED7.cathode
  N16: R12.Pin_1, LED14.cathode
  N17: R13.Pin_1, LED8.cathode
  N18: R14.Pin_1, LED15.cathode
  N19: R15.Pin_1, LED9.cathode
  N20: R16.Pin_1, LED10.cathode
  N21: LED1.anode, U2.ST_CP
  N22: LED2.anode, U2.SH_CP
  N23: LED4.anode, U2.MR
  N24: LED6.anode, U1.Q0
  N25: LED7.anode, U1.DS
  N26: LED8.anode, U1.OE
  N27: LED9.anode, U1.ST_CP
  N28: LED10.anode, U1.SH_CP
  N29: LED11.anode, U1.MR
  N30: LED12.anode, U1.Q7'
  N31: LED13.anode, U2.OE
  N32: LED14.anode, U2.DS
  N33: LED15.anode, U2.Q0
  N34: LED16.anode, U2.Q7'
  N35: R17.Pin_1, LED17.cathode
  N36: LED17.anode, U1.Q7
  N37: U1.Q1, U2.Q6
  GND: U1.Q2, U1.GND, U2.Q2, U2.GND
  VCC: U1.Q5, U1.VCC, U2.Q5, U2.VCC
