# Fritzing sketch MIC_OA (saved by Fritzing 0.7.12b)
breadboards: 1

parts:
  Arduino1 = Arduino
  MIC1 = Microphone
  R1 = 2.2k Ω Resistor [package=THT]
  R2 = 68k Ω Resistor [package=THT]
  R3 = 100k Ω Resistor [package=THT]
  R4 = 1k Ω Resistor [package=THT]
  C1 = Ceramic Capacitor [package=THT]
  U1 = LM 358 Dual Op-Amp [package="DIP8 [THT]"]

nets:
  N1: Arduino1.+5V, R1.Pin_0, U1.connector7
  N2: Arduino1.GND, MIC1.pin1, R4.Pin_1, U1.connector3
  N3: Arduino1.A0, R3.Pin_1, U1.connector0
  N4: MIC1.pin2, R1.Pin_1, C1.pin_0
  N5: R2.Pin_0, C1.pin_1, U1.connector2
  N6: R3.Pin_0, R4.Pin_0, U1.connector1
