# Fritzing sketch PhotoResistor (saved by Fritzing 0.7.0b)
breadboards: 1

parts:
  Arduino1 = Arduino
  LED1 = LED - 5mm [color="Red (633nm)" package="5 mm [THT]"]
  R1 = Photocell (LDR) [package=THT]
  R2 = Resistor [tolerance=±5% resistance=220 package=THT]

nets:
  N1: Arduino1.GND, LED1.cathode, R2.Pin_1
  N2: Arduino1.D13, LED1.anode
  N3: Arduino1.+5V, R1.pin_0
  N4: Arduino1.A0, R1.pin_1, R2.Pin_0
