# Fritzing sketch RTC_DS1307 (saved by Fritzing 0.7.11b)
breadboards: 1

parts:
  Arduino1 = Arduino
  IC1 = DS1307 [package=THT]
  C1 = Ceramic Capacitor [package=THT]
  XTAL1 = CRYSTAL - kHz [frequency="32 kHz"]
  VCC1 = Battery

nets:
  N1: Arduino1.+5V, IC1.+V, C1.pin_1
  N2: Arduino1.GND, IC1.0V, C1.pin_0, VCC1.-
  N3: Arduino1.A4, IC1.SDA_-_I2C_Data
  N4: Arduino1.A5, IC1.SCL_-_I2C_Clock
  N5: IC1.X1_-_Crystal, XTAL1.pin_1
  N6: IC1.X2_-_Crystal, XTAL1.pin_0
  N7: IC1.Vbat_-_Backup_Supply, VCC1.+
