# Fritzing sketch SevenSegment4in1 (saved by Fritzing 0.8.3b)
breadboards: 1

parts:
  元件1 = Arduino Uno (Rev3)
  U1 = 7-SEGMENT-4DIGIT [package=7-segment-4digit-youngsun]

nets:
  N1: 元件1.D8, U1.9
  N2: 元件1.D10_PWM/SS, U1.11
  N3: 元件1.D12/MISO, U1.13
  N4: 元件1.D13/SCK, U1.14
  N5: 元件1.D2, U1.8
  N6: 元件1.D3_PWM, U1.7
  N7: 元件1.D4, U1.6
  N8: 元件1.D5_PWM, U1.5
  N9: 元件1.D6_PWM, U1.4
  N10: 元件1.D7, U1.3
