# Fritzing sketch SimonSays (saved by Fritzing 0.7.0b)
breadboards: 1

parts:
  Arduino1 = Arduino
  S1 = Pushbutton [package="[THT]"]
  S2 = Pushbutton [package="[THT]"]
  S3 = Pushbutton [package="[THT]"]
  S4 = Pushbutton [package="[THT]"]
  R1 = Resistor [tolerance=±5% resistance=220 package=THT]
  LED1 = LED - 5mm [color="Red (633nm)" package="5 mm [THT]"]
  LED2 = LED - 5mm [color="Red (633nm)" package="5 mm [THT]"]
  LED3 = LED - 5mm [color="Red (633nm)" package="5 mm [THT]"]
  LED4 = LED - 5mm [color="Red (633nm)" package="5 mm [THT]"]
  R2 = Resistor [tolerance=±5% resistance=220 package=THT]
  R3 = Resistor [tolerance=±5% resistance=220 package=THT]
  R4 = Resistor [tolerance=±5% resistance=220 package=THT]
  R5 = Rotary Potentiometer (Small) [maximum_resistance=100kΩ]
  SPKR1 = Loudspeaker

nets:
  N1: Arduino1.D11, R1.Pin_0
  N2: Arduino1.D10, R2.Pin_0
  N3: Arduino1.D9, R3.Pin_0
  N4: Arduino1.D8, R4.Pin_0
  N5: Arduino1.D5, S3.Pin_1, S3.Pin_2
  N6: Arduino1.D4, S4.Pin_1, S4.Pin_2
  N7: Arduino1.D3, S1.Pin_1, S1.Pin_2
  N8: Arduino1.D2, S2.Pin_1, S2.Pin_2
  N9: Arduino1.GND, S1.Pin_3, S1.Pin_4, S2.Pin_3, S2.Pin_4, S3.Pin_3, S3.Pin_4, S4.Pin_3, S4.Pin_4, LED1.cathode, LED2.cathode, LED3.cathode, LED4.cathode, SPKR1.pin1
  N10: Arduino1.A0, R5.leg2
  N11: R1.Pin_1, LED1.anode
  N12: LED2.anode, R2.Pin_1
  N13: LED3.anode, R3.Pin_1
  N14: LED4.anode, R4.Pin_1
  N15: R5.wiper, SPKR1.pin2
