# Fritzing sketch SwitchLed (saved by Fritzing 0.7.0b)
breadboards: 1

parts:
  Arduino1 = Arduino
  S1 = Pushbutton [package="[THT]"]  # not connected
  R1 = Resistor [tolerance=±5% resistance=220 package=THT]

nets:
  N1: Arduino1.D2, R1.Pin_0
  N2: Arduino1.GND, R1.Pin_1
