# Fritzing sketch game_typing (saved by Fritzing 0.9.2b)
breadboards: 1

parts:
  LCD1 = LCD screen  # not connected
  元件2 = Arduino Uno (Rev3)
  SG1 = Buzzer 12mm [package=buzzer-12mm-ns]

nets:
  N1: 元件2.D5_PWM, SG1.1
  N2: 元件2.GND, SG1.2

notes:
  5
  長腳或紅線
  短腳或黑線
  GND
  VCC
  SDA
  SCL
  A5
  2
  A4
