# Fritzing sketch rtttl (saved by Fritzing 0.9.1b)

parts:
  元件1 = Arduino Uno (Rev3)
  R1 = Resistor [tolerance=±5% resistance=100 package=THT]
  SP1 = SPEAKER [package=pcb_mount_speaker]

nets:
  N1: 元件1.GND, SP1.+
  N2: 元件1.D3_PWM, R1.Pin_1
  N3: R1.Pin_0, SP1.-
